# Fritzing sketch parking1 (saved by Fritzing 0.9.3b)
breadboards: 2

parts:
  M2 = fc-51 [package=THT]
  module1 = I2C LCD1602
  VCC1 = Battery
  WeMos_D1_R1 = WeMos D1 R2
  M3 = fc-51 [package=THT]
  M4 = fc-51 [package=THT]
  M5 = fc-51 [package=THT]
  J1 = Basic Servo
  J2 = Basic Servo
  Part1 = Arduino Ethernet Shield (Rev3)
  Part2 = RFID-RC522-v2
  Part3 = RFID-RC522-v2

nets:
  N1: M2.pin1, WeMos_D1_R1.D0/RX
  GND: M2.pin2, module1.GND, VCC1.-, WeMos_D1_R1.GND, M3.pin2, M4.pin2, M5.pin2, J1.gnd, J2.gnd
  VCC: M2.pin3, VCC1.+, WeMos_D1_R1.VIN, M3.pin3, M4.pin3, M5.pin3, J1.vcc, J2.vcc
  N2: module1.SCL, WeMos_D1_R1.D15
  N3: module1.SDA, WeMos_D1_R1.D14
  VCC_2: module1.VCC, WeMos_D1_R1.5V
  N4: WeMos_D1_R1.D3, M3.pin1
  N5: WeMos_D1_R1.D4, M4.pin1
  N6: WeMos_D1_R1.(D5), M5.pin1
  N7: WeMos_D1_R1.(D6), J1.pulse
  N8: WeMos_D1_R1.(D7), J2.pulse
  N9: Part1.PWM_D9, Part2.RST, Part3.RST
  N10: Part1.SPI/D12, Part2.IRQ, Part3.MISO
  N11: Part1.SPI/D13, Part2.SCK, Part3.SCK
  3.3V: Part1.3V3, Part2.3.3V, Part3.3.3V
  GND_2: Part1.GND, Part2.GND, Part3.GND

custom parts:
  I2C LCD1602: I2C LCD1602 module of ZHIYU Sensor Kit
  Battery: Your standard 2x 18650 battery pack (7.4 Volts)
  WeMos D1 R2: The D1 R2 is a mini wifi board based on the ESP-8266EX.
  RFID-RC522-v2: A simple China made RFID-RC522 Reader; do check the pin labels, as this is a MFRC522 based clone.
